// Logisim project lAB2-EXERCISE 1.circ as structural Verilog: 1 circuit, main circuit main
module main (
  input  in_1,
  input  in_2,
  input  in_3,
  input  in_4,
  output out_5,
  output out_6,
  output out_7,
  output out_8
);

  wire and_2_out, not_1_out;

  not not_1 (not_1_out, in_3);
  xor xor_1 (out_5, in_1, in_2);
  and and_1 (out_6, in_1, in_2);
  xor xor_2 (out_7, in_3, in_4);
  and and_2 (and_2_out, in_4, not_1_out);

  // Notes on the sheet:
  //   Half Adder
  //   Half Subtracter
endmodule
